# Fritzing sketch pedalera (saved by Fritzing 0.9.5d)
circuit board: 8.46667cm x 5.64444cm
breadboards: 1

parts:
  Componente1 = Arduino Leonardo (Rev3b)
  LED2 = LED - 5mm [color="Red (633nm)" package="5 mm [THT]"]
  LED3 = LED - 5mm [color="Red (633nm)" package="5 mm [THT]"]
  LED4 = LED - 5mm [color="Red (633nm)" package="5 mm [THT]"]
  LED5 = LED - 5mm [color="Red (633nm)" package="5 mm [THT]"]
  LED6 = LED - 5mm [color="Red (633nm)" package="5 mm [THT]"]
  LED7 = LED - 5mm [color="Red (633nm)" package="5 mm [THT]"]
  LED8 = LED - 5mm [color="Red (633nm)" package="5 mm [THT]"]
  LED9 = LED - 5mm [color="Red (633nm)" package="5 mm [THT]"]
  S1 = Pushbutton [package="[THT]"]
  S2 = Pushbutton [package="[THT]"]
  S3 = Pushbutton [package="[THT]"]
  S4 = Pushbutton [package="[THT]"]
  S5 = Pushbutton [package="[THT]"]
  S6 = Pushbutton [package="[THT]"]
  S7 = Pushbutton [package="[THT]"]
  S8 = Pushbutton [package="[THT]"]
  U1 = MIDI_CONN_FEMALE_SUPPORT [package=din_5_female_support]
  R11 = Resistor [tolerance=±5% resistance=10k package=THT]
  R12 = Resistor [tolerance=±5% resistance=10k package=THT]
  R14 = Resistor [tolerance=±5% resistance=10k package=THT]
  R15 = Resistor [tolerance=±5% resistance=10k package=THT]
  R16 = Resistor [tolerance=±5% resistance=10k package=THT]
  R17 = Resistor [tolerance=±5% resistance=10k package=THT]
  R18 = Resistor [tolerance=±5% resistance=10k package=THT]
  R10 = Resistor [tolerance=±5% resistance=220 package=THT]
  R9 = Resistor [tolerance=±5% resistance=220 package=THT]
  R1 = Resistor [tolerance=±5% resistance=220 package=THT]
  R2 = Resistor [tolerance=±5% resistance=220 package=THT]
  R3 = Resistor [tolerance=±5% resistance=220 package=THT]
  R4 = Resistor [tolerance=±5% resistance=220 package=THT]
  R5 = Resistor [tolerance=±5% resistance=220 package=THT]
  R6 = Resistor [tolerance=±5% resistance=220 package=THT]
  R7 = Resistor [tolerance=±5% resistance=220 package=THT]
  R8 = Resistor [tolerance=±5% resistance=220 package=THT]
  R19 = Resistor [tolerance=±5% resistance=10k package=THT]

nets (from the breadboard view):
  N1: Componente1.D1/TX, R9.Pin_1
  N2: Componente1.D4/A6, S1.Pin_1, S1.Pin_2, R11.Pin_0
  N3: Componente1.D5_PWM, S2.Pin_1, S2.Pin_2, R12.Pin_0
  N4: Componente1.D6_PWM/A7, S3.Pin_1, S3.Pin_2, R19.Pin_0
  N5: Componente1.D7, S4.Pin_1, S4.Pin_2, R14.Pin_0
  N6: Componente1.5V, R10.Pin_1
  N7: Componente1.GND, LED2.cathode, LED3.cathode, LED4.cathode, LED5.cathode, LED6.cathode, LED7.cathode, LED8.cathode, LED9.cathode, U1.NC1, R11.Pin_1, R12.Pin_1, R14.Pin_1, R15.Pin_1, R16.Pin_1, R17.Pin_1, R18.Pin_1, R19.Pin_1
  N8: Componente1.A0, R3.Pin_1
  N9: Componente1.A1, R4.Pin_1
  N10: Componente1.A2, R5.Pin_1
  N11: Componente1.A3, R6.Pin_1
  N12: Componente1.A4, R7.Pin_1
  N13: Componente1.A5, R8.Pin_1
  N14: Componente1.D8/A8, S5.Pin_1, S5.Pin_2, R15.Pin_0
  N15: Componente1.D9_PWM/A9, S6.Pin_1, S6.Pin_2, R16.Pin_0
  N16: Componente1.D10_PWM/A10, S7.Pin_1, S7.Pin_2, R17.Pin_0
  N17: Componente1.D11_PWM, S8.Pin_1, S8.Pin_2, R18.Pin_0
  N18: Componente1.D12/A11, R1.Pin_1
  N19: Componente1.D13_PWM, R2.Pin_1
  N20: LED2.anode, R1.Pin_0
  N21: LED3.anode, R2.Pin_0
  N22: LED4.anode, R3.Pin_0
  N23: LED5.anode, R4.Pin_0
  N24: LED6.anode, R5.Pin_0
  N25: LED7.anode, R6.Pin_0
  N26: LED8.anode, R7.Pin_0
  N27: LED9.anode, R8.Pin_0
  N28: S1.Pin_3, S1.Pin_4, S2.Pin_3, S2.Pin_4, S3.Pin_3, S3.Pin_4, S4.Pin_3, S4.Pin_4, S5.Pin_3, S5.Pin_4, S6.Pin_3, S6.Pin_4, S7.Pin_3, S7.Pin_4, S8.Pin_3, S8.Pin_4
  N29: U1.MIDI_IN, R9.Pin_0
  N30: U1.MIDI_OUT, R10.Pin_0
