# Fritzing sketch pedalera_mega2 (saved by Fritzing 0.9.5d)
circuit board: 8.46667cm x 5.64444cm
breadboards: 1

parts:
  LED2 = LED - 5mm [color="Red (633nm)" package="5 mm [THT]"]
  LED3 = LED - 5mm [color="Red (633nm)" package="5 mm [THT]"]
  LED4 = LED - 5mm [color="Red (633nm)" package="5 mm [THT]"]
  LED5 = LED - 5mm [color="Red (633nm)" package="5 mm [THT]"]
  LED6 = LED - 5mm [color="Red (633nm)" package="5 mm [THT]"]
  LED7 = LED - 5mm [color="Red (633nm)" package="5 mm [THT]"]
  LED8 = LED - 5mm [color="Red (633nm)" package="5 mm [THT]"]
  LED9 = LED - 5mm [color="Red (633nm)" package="5 mm [THT]"]
  S1 = Pushbutton [package="[THT]"]
  S2 = Pushbutton [package="[THT]"]
  S3 = Pushbutton [package="[THT]"]
  S4 = Pushbutton [package="[THT]"]
  S5 = Pushbutton [package="[THT]"]
  S6 = Pushbutton [package="[THT]"]
  S7 = Pushbutton [package="[THT]"]
  S8 = Pushbutton [package="[THT]"]
  U1 = MIDI_CONN_FEMALE_SUPPORT [package=din_5_female_support]
  R11 = Resistor [tolerance=±5% resistance=10k package=THT]
  R12 = Resistor [tolerance=±5% resistance=10k package=THT]
  R14 = Resistor [tolerance=±5% resistance=10k package=THT]
  R15 = Resistor [tolerance=±5% resistance=10k package=THT]
  R16 = Resistor [tolerance=±5% resistance=10k package=THT]
  R17 = Resistor [tolerance=±5% resistance=10k package=THT]
  R18 = Resistor [tolerance=±5% resistance=10k package=THT]
  R10 = Resistor [tolerance=±5% resistance=220 package=THT]
  R1 = Resistor [tolerance=±5% resistance=220 package=THT]
  R2 = Resistor [tolerance=±5% resistance=220 package=THT]
  R3 = Resistor [tolerance=±5% resistance=220 package=THT]
  R4 = Resistor [tolerance=±5% resistance=220 package=THT]
  R5 = Resistor [tolerance=±5% resistance=220 package=THT]
  R6 = Resistor [tolerance=±5% resistance=220 package=THT]
  R7 = Resistor [tolerance=±5% resistance=220 package=THT]
  R8 = Resistor [tolerance=±5% resistance=220 package=THT]
  R19 = Resistor [tolerance=±5% resistance=10k package=THT]
  L1 = Inductor [package="400 mil [THT]"]
  L2 = Inductor [package="400 mil [THT]"]
  Componente1 = Arduino Mega 2560 (Rev3)

nets (from the breadboard view):
  N1: LED2.cathode, LED3.cathode, LED4.cathode, LED5.cathode, LED6.cathode, LED7.cathode, LED8.cathode, LED9.cathode, U1.NC1, R11.Pin_1, R12.Pin_1, R14.Pin_1, R15.Pin_1, R16.Pin_1, R17.Pin_1, R18.Pin_1, R19.Pin_1, Componente1.GND
  N2: LED2.anode, R1.Pin_0
  N3: LED3.anode, R2.Pin_0
  N4: LED4.anode, R3.Pin_0
  N5: LED5.anode, R4.Pin_0
  N6: LED6.anode, R5.Pin_0
  N7: LED7.anode, R6.Pin_0
  N8: LED8.anode, R7.Pin_0
  N9: LED9.anode, R8.Pin_0
  N10: S1.Pin_1, S1.Pin_2, R11.Pin_0, Componente1.D46
  N11: S1.Pin_3, S1.Pin_4, S2.Pin_3, S2.Pin_4, S3.Pin_3, S3.Pin_4, S4.Pin_3, S4.Pin_4, S5.Pin_3, S5.Pin_4, S6.Pin_3, S6.Pin_4, S7.Pin_3, S7.Pin_4, S8.Pin_3, S8.Pin_4
  N12: S2.Pin_1, S2.Pin_2, R12.Pin_0, Componente1.D47
  N13: S3.Pin_1, S3.Pin_2, R19.Pin_0, Componente1.D48
  N14: S4.Pin_1, S4.Pin_2, R14.Pin_0, Componente1.D49
  N15: S5.Pin_1, S5.Pin_2, R15.Pin_0, Componente1.D50
  N16: S6.Pin_1, S6.Pin_2, R16.Pin_0, Componente1.D51
  N17: S7.Pin_1, S7.Pin_2, R17.Pin_0, Componente1.D52
  N18: S8.Pin_1, S8.Pin_2, R18.Pin_0, Componente1.D53
  N19: U1.MIDI_IN, L2.pin_0
  N20: U1.MIDI_OUT, R10.Pin_0
  N21: R10.Pin_1, L1.pin_0
  N22: R1.Pin_1, Componente1.D22
  N23: R2.Pin_1, Componente1.D23
  N24: R3.Pin_1, Componente1.D24
  N25: R4.Pin_1, Componente1.D25
  N26: R5.Pin_1, Componente1.D27
  N27: R6.Pin_1, Componente1.D26
  N28: R7.Pin_1, Componente1.D28
  N29: R8.Pin_1, Componente1.D29
  N30: L1.pin_1, Componente1.5V
  N31: L2.pin_1, Componente1.D1_TX0

notes:
  1
